# Fritzing sketch Untitled Sketch 2 (saved by Fritzing 0.8.7b)

parts:
  RFM95W1 = RFM95W LoRa Module
  MCU1 = STM32 Blue Pill [part_number=STM32F103C8T6]
  Part1 = FTDI Basic Programmer

nets:
  N1: RFM95W1.2_MISO, MCU1.pin31
  N2: RFM95W1.3_MOSI, MCU1.pin32
  N3: RFM95W1.4_SCK, MCU1.pin30
  N4: RFM95W1.5_NSS_(CS), MCU1.pin29
  N5: RFM95W1.6_RESET, MCU1.pin33
  N6: RFM95W1.10_GND, MCU1.pin19, MCU1.pin_40, Part1.GND
  N7: RFM95W1.13_3.3V, MCU1.pin38
  N8: RFM95W1.14_DIO0, MCU1.pin28
  N9: RFM95W1.15_DIO1, MCU1.pin13
  N10: MCU1.pin6, Part1.RXI
  N11: MCU1.pin7, Part1.TXO
  N12: MCU1.pin18, Part1.POWER

custom parts:
  RFM95W LoRa Module: RF Transceiver by Hope RF. Well supported Arduino libraries are available. This Low Power Long Range Transceiver Module for the frequencies 868MHz and 915MHz and it is also available in other versions.
  STM32 Blue Pill: The STM32 family of 32-bit microcontrollers based on the Arm Cortex-M processor is designed to offer new degrees of freedom to MCU users. It offers products combining very high performance, real-time capabilities, digital signal processing, low-power / low-voltage operation, and connectivity, while maintaining full integration and ease of development.
